# Fritzing sketch Схема (saved by Fritzing 0.9.3b)

parts:
  Часть1 = Arduino Nano (Rev3.0)
  OLED = Grove OLED 128x96
  SPK = Piezo Speaker
  C1 = Ceramic Capacitor [capacitance=1µF package="100 mil [THT, multilayer]"]
  R2 = Resistor [tolerance=±5% resistance=10k package=THT]
  R3 = Resistor [tolerance=±5% resistance=5k package=THT]
  R4 = Resistor [tolerance=±5% resistance=10k package=THT]
  R1 = Resistor [tolerance=±5% resistance=5k package=THT]

nets:
  GND: Часть1.GND, OLED.GND, SPK.pin1, R3.Pin_1, R1.Pin_0
  N1: Часть1.D8, OLED.SDA
  N2: Часть1.D9, OLED.SCL
  N3: Часть1.D10, C1.1
  N4: Часть1.D11/MOSI, R2.Pin_1, R1.Pin_1
  5V: Часть1.5V, OLED.VCC
  N5: Часть1.A0, R3.Pin_0, R4.Pin_0
  N6: SPK.pin2, C1.0

notes:
  +12V ближний свет
  +12V от АКБ
  GND
